# Fritzing sketch Sketch (saved by Fritzing 0.9.3b)
breadboards: 1

parts:
  Onderdeel1 = Arduino Mega ADK (Rev3)
  LCD1 = LCD screen  # not connected
  HC-SR04_Sensor_1 = HC-SR04 Ultrasonic Distance Sensor

nets:
  5V: Onderdeel1.5V, HC-SR04_Sensor_1.VCC
  GND: Onderdeel1.GND, HC-SR04_Sensor_1.GND
  N1: Onderdeel1.D2_PWM, HC-SR04_Sensor_1.TRIG
  N2: Onderdeel1.D3_PWM, HC-SR04_Sensor_1.ECHO
